// Logisim project arithmetic-Add.circ as structural Verilog: 1 circuit, main circuit main
module main (
  output [7:0] result,
  output halt
);

  wire N3;

  Adder #(.width(8)) adder_1 (.a(8'hc), .b(8'h3), .out(result), .cin(1'b0), .cout(N3));

  assign halt = 1'b1;

  // Other names for the same wires on the sheet: N2[7:0] = result
endmodule
