// Logisim project arithmetic-BitAdder.circ as structural Verilog: 1 circuit, main circuit main
module main (
  output [3:0] result,
  output halt
);

  BitAdder #(.numInputs(1), .width(8)) bitadder_1 (.in0(8'hc), .out(result));

  assign halt = 1'b1;

  // Other names for the same wires on the sheet: N1[3:0] = result
endmodule
