// Logisim project arithmetic-BitFinder.circ as structural Verilog: 1 circuit, main circuit main
module main (
  output [2:0] result,
  output halt
);

  wire N2;

  BitFinder #(.\type ("low1"), .width(8)) bitfinder_1 (.in(8'hc), .index(result), .found(N2));

  assign halt = 1'b1;

  // Other names for the same wires on the sheet: N1[2:0] = result
endmodule
