// Logisim project arithmetic-Compare.circ as structural Verilog: 1 circuit, main circuit main
module main (
  output result,
  output halt
);

  wire N2, N3;

  Comparator #(.mode("unsigned"), .width(8)) comparator_1 (.a(8'hc), .b(8'h3), .gt(result), .eq(N3), .lt(N2));

  assign halt = 1'b1;

  // Other names for the same wires on the sheet: N4 = result
endmodule
