// Logisim project arithmetic-Divide.circ as structural Verilog: 1 circuit, main circuit main
module main (
  output [7:0] result,
  output halt
);

  Divider #(.width(8)) divider_1 (.a(8'hc), .b(8'h3), .out(result), .upper({8{1'b0}}));  // open: rem

  assign halt = 1'b1;

  // Other names for the same wires on the sheet: N2[7:0] = result
endmodule
