// Logisim project arithmetic-Multiply.circ as structural Verilog: 1 circuit, main circuit main
module main (
  output [7:0] result,
  output halt
);

  Multiplier #(.width(8)) multiplier_1 (.a(8'hc), .b(8'h3), .out(result), .cin({8{1'b0}}));  // open: cout

  assign halt = 1'b1;

  // Other names for the same wires on the sheet: N2[7:0] = result
endmodule
