// Logisim project arithmetic-Subtract.circ as structural Verilog: 1 circuit, main circuit main
module main (
  output [7:0] result,
  output halt
);

  wire N3;

  Subtractor #(.width(8)) subtractor_1 (.a(8'hc), .b(8'h3), .out(result), .bin(1'b0), .bout(N3));

  assign halt = 1'b1;

  // Other names for the same wires on the sheet: N2[7:0] = result
endmodule
