// Logisim project counter-sequence.circ as structural Verilog: 1 circuit, main circuit main
module main (
  output [3:0] result,
  output halt
);

  wire N0;

  Clock #(.highDuration(1), .lowDuration(1), .width(1)) clock_1 (.out(N0));
  Counter #(.max('h3), .ongoal("wrap"), .trigger("rising"), .width(4)) counter_1 (
    .load(1'b0), .D(4'b0000), .count(1'b1), .Q(result), .carry(halt), .clk(N0), .clr(1'b0));

  // Other names for the same wires on the sheet: N3[3:0] = result; N4 = halt
endmodule
