// Logisim project extra-BitSelector.circ as structural Verilog: 1 circuit, main circuit main
module main (
  output [1:0] result,
  output halt
);

  BitSelector #(.group(2), .width(8)) bitselector_1 (.in(8'ha5), .out(result), .sel(2'b01));

  assign halt = 1'b1;

  // Other names for the same wires on the sheet: N2[1:0] = result
endmodule
