// Logisim project extra-ControlledInverter.circ as structural Verilog: 2 circuits, main circuit main
module main (
  output [7:0] result,
  output halt
);

  Practice_ActiveLow_p1 practice_activelow_p1_1 (.A(8'ha5), .EN(1'b0), .Y(result));

  assign halt = 1'b1;

  // Other names for the same wires on the sheet: N2[7:0] = result
endmodule

module Practice_ActiveLow_p1 (
  input  [7:0] A,
  input  EN,
  output [7:0] Y
);

  wire N3;

  assign Y = N3 ? ~A : 8'bz;  // Controlled_Inverter controlled_inverter_1
  not not_1 (N3, EN);

  // Other names for the same wires on the sheet: N0[7:0] = A; N1 = EN; N2[7:0] = Y
endmodule
