// Logisim project extra-EvenParity.circ as structural Verilog: 2 circuits, main circuit main
module main (
  output result,
  output halt
);

  Practice_ParityBits_p1 practice_paritybits_p1_1 (.A(8'ha5), .Y(result));

  assign halt = 1'b1;

  // Other names for the same wires on the sheet: N1 = result
endmodule

module Practice_ParityBits_p1 (
  input  [7:0] A,
  output Y
);

  xnor xnor_1 (Y, A[0], A[1], A[2], A[3], A[4], A[5], A[6], A[7]);

  // Other names for the same wires on the sheet: N0[7:0] = A; N2 = A[0]; N3 = A[1]; N4 = A[2]; N5 = A[3]; N6 = A[4];
  //   N7 = A[5]; N8 = A[6]; N9 = A[7]; N1 = Y
endmodule
