// Logisim project extra-ShiftRight.circ as structural Verilog: 2 circuits, main circuit main
module main (
  output [7:0] result,
  output halt
);

  Practice_BarrelShift_p1 practice_barrelshift_p1_1 (.A(8'ha5), .B(8'h2), .Y(result));

  assign halt = 1'b1;

  // Other names for the same wires on the sheet: N2[7:0] = result
endmodule

module Practice_BarrelShift_p1 (
  input  [7:0] A,
  input  [7:0] B,
  output [7:0] Y
);

  wire N20, N21, N22, N23, N24, N25, N26, N27, N28, N29, N30, N31, N32, N33, N34, N35, N36, N37, N38, N39,
       N40, N41, N42, N43, N45;

  Multiplexer #(.enable("false"), .select(1), .tristate("false"), .width(1)) multiplexer_1 (
    .in0(A[2]), .in1(A[3]), .out(N22), .sel(B[0]));
  Multiplexer #(.enable("false"), .select(1), .tristate("false"), .width(1)) multiplexer_2 (
    .in0(N22), .in1(N24), .out(N30), .sel(B[1]));
  Multiplexer #(.enable("false"), .select(1), .tristate("false"), .width(1)) multiplexer_3 (
    .in0(N30), .in1(N34), .out(N38), .sel(B[2]));
  Multiplexer #(.enable("false"), .select(1), .tristate("false"), .width(8)) multiplexer_4 (
    .in0({N43, N42, N41, N40, N39, N38, N37, N36}), .in1({8{1'b0}}), .out(Y), .sel(N45));
  Multiplexer #(.enable("false"), .select(1), .tristate("false"), .width(1)) multiplexer_5 (
    .in0(A[3]), .in1(A[4]), .out(N23), .sel(B[0]));
  Multiplexer #(.enable("false"), .select(1), .tristate("false"), .width(1)) multiplexer_6 (
    .in0(N23), .in1(N25), .out(N31), .sel(B[1]));
  Multiplexer #(.enable("false"), .select(1), .tristate("false"), .width(1)) multiplexer_7 (
    .in0(N31), .in1(N35), .out(N39), .sel(B[2]));
  Multiplexer #(.enable("false"), .select(1), .tristate("false"), .width(1)) multiplexer_8 (
    .in0(A[4]), .in1(A[5]), .out(N24), .sel(B[0]));
  Multiplexer #(.enable("false"), .select(1), .tristate("false"), .width(1)) multiplexer_9 (
    .in0(N24), .in1(N26), .out(N32), .sel(B[1]));
  Multiplexer #(.enable("false"), .select(1), .tristate("false"), .width(1)) multiplexer_10 (
    .in0(N32), .in1(1'b0), .out(N40), .sel(B[2]));
  Multiplexer #(.enable("false"), .select(1), .tristate("false"), .width(1)) multiplexer_11 (
    .in0(A[5]), .in1(A[6]), .out(N25), .sel(B[0]));
  Multiplexer #(.enable("false"), .select(1), .tristate("false"), .width(1)) multiplexer_12 (
    .in0(N25), .in1(N27), .out(N33), .sel(B[1]));
  Multiplexer #(.enable("false"), .select(1), .tristate("false"), .width(1)) multiplexer_13 (
    .in0(N33), .in1(1'b0), .out(N41), .sel(B[2]));
  Multiplexer #(.enable("false"), .select(1), .tristate("false"), .width(1)) multiplexer_14 (
    .in0(A[6]), .in1(A[7]), .out(N26), .sel(B[0]));
  Multiplexer #(.enable("false"), .select(1), .tristate("false"), .width(1)) multiplexer_15 (
    .in0(N26), .in1(1'b0), .out(N34), .sel(B[1]));
  Multiplexer #(.enable("false"), .select(1), .tristate("false"), .width(1)) multiplexer_16 (
    .in0(N34), .in1(1'b0), .out(N42), .sel(B[2]));
  Multiplexer #(.enable("false"), .select(1), .tristate("false"), .width(1)) multiplexer_17 (
    .in0(A[7]), .in1(1'b0), .out(N27), .sel(B[0]));
  Multiplexer #(.enable("false"), .select(1), .tristate("false"), .width(1)) multiplexer_18 (
    .in0(N27), .in1(1'b0), .out(N35), .sel(B[1]));
  Multiplexer #(.enable("false"), .select(1), .tristate("false"), .width(1)) multiplexer_19 (
    .in0(N35), .in1(1'b0), .out(N43), .sel(B[2]));
  Multiplexer #(.enable("false"), .select(1), .tristate("false"), .width(1)) multiplexer_20 (
    .in0(A[0]), .in1(A[1]), .out(N20), .sel(B[0]));
  Multiplexer #(.enable("false"), .select(1), .tristate("false"), .width(1)) multiplexer_21 (
    .in0(N20), .in1(N22), .out(N28), .sel(B[1]));
  Multiplexer #(.enable("false"), .select(1), .tristate("false"), .width(1)) multiplexer_22 (
    .in0(N28), .in1(N32), .out(N36), .sel(B[2]));
  Multiplexer #(.enable("false"), .select(1), .tristate("false"), .width(1)) multiplexer_23 (
    .in0(A[1]), .in1(A[2]), .out(N21), .sel(B[0]));
  Multiplexer #(.enable("false"), .select(1), .tristate("false"), .width(1)) multiplexer_24 (
    .in0(N21), .in1(N23), .out(N29), .sel(B[1]));
  Multiplexer #(.enable("false"), .select(1), .tristate("false"), .width(1)) multiplexer_25 (
    .in0(N29), .in1(N33), .out(N37), .sel(B[2]));
  or or_1 (N45, B[3], B[4], B[5], B[6], B[7]);

  // Other names for the same wires on the sheet: N0[7:0] = A; N3 = A[0]; N4 = A[1]; N5 = A[2]; N6 = A[3]; N7 = A[4];
  //   N8 = A[5]; N9 = A[6]; N10 = A[7]; N1[7:0] = B; N11 = B[0]; N12 = B[1]; N13 = B[2]; N14 = B[3]; N15 = B[4];
  //   N16 = B[5]; N17 = B[6]; N18 = B[7]; N2[7:0] = Y; N44[7:0] = {N43, N42, N41, N40, N39, N38, N37, N36}
endmodule
