// Logisim project gate-rotation-0.circ as structural Verilog: 1 circuit, main circuit main
module main (
  output [7:0] result,
  output halt
);

  assign result = {8{1'b1}} & ~8'hf & 8'haa;  // AND_Gate and_1, 8 bits wide

  assign halt = 1'b1;

  // Other names for the same wires on the sheet: N3[7:0] = result
endmodule
