// Logisim project memory-ROM.circ as structural Verilog: 1 circuit, main circuit main
module main (
  output [7:0] result,
  output halt
);

  ROM #(.addrWidth(4), .dataWidth(8)) rom_1 (.addr(4'b0011), .data(result), .sel(1'b1));

  assign halt = 1'b1;

  // Other names for the same wires on the sheet: N1[7:0] = result

  // Notes on the sheet:
  //   contents of rom_1 (hex, n*v repeats v):
  //   0 0 0 a5
endmodule
