// Logisim project reverse-join.circ as structural Verilog: 2 circuits, main circuit main
module main (
  output [7:0] result,
  output halt
);

  Practice_BitMapping_p1 practice_bitmapping_p1_1 (.B0(4'b1111), .B1(4'b0000), .Y(result));

  assign halt = 1'b1;

  // Other names for the same wires on the sheet: N2[7:0] = result
endmodule

module Practice_BitMapping_p1 (
  input  [3:0] B0,
  input  [3:0] B1,
  output [7:0] Y
);


  assign Y = {B0[0], B1[0], B0[2], B1[2], B1[3], B0[3], B1[1], B0[1]};

  // Other names for the same wires on the sheet: N0[3:0] = B0;
  //   N2[7:0] = {B0[0], B1[0], B0[2], B1[2], B1[3], B0[3], B1[1], B0[1]}; N10 = B0[0]; N3 = B0[1]; N8 = B0[2];
  //   N5 = B0[3]; N1[3:0] = B1; N9 = B1[0]; N4 = B1[1]; N7 = B1[2]; N6 = B1[3]
endmodule
