// Logisim project reverse-split.circ as structural Verilog: 2 circuits, main circuit main
module main (
  output [3:0] result,
  output halt
);

  wire [3:0] N2;

  Practice_BitMapping_p1 practice_bitmapping_p1_1 (.A(8'ha5), .B0(result), .B1(N2));

  assign halt = 1'b1;

  // Other names for the same wires on the sheet: N1[3:0] = result
endmodule

module Practice_BitMapping_p1 (
  input  [7:0] A,
  output [3:0] B0,
  output [3:0] B1
);


  assign B0 = {A[2], A[5], A[0], A[7]};
  assign B1 = {A[3], A[4], A[1], A[6]};

  // Other names for the same wires on the sheet: N0[7:0] = A; N1[3:0] = {A[2], A[5], A[0], A[7]}; N10 = A[7];
  //   N3 = A[0]; N8 = A[5]; N5 = A[2]; N2[3:0] = {A[3], A[4], A[1], A[6]}; N9 = A[6]; N4 = A[1]; N7 = A[4]; N6 = A[3]
endmodule
