// Logisim project select-Decoder.circ as structural Verilog: 1 circuit, main circuit main
module main (
  output result,
  output halt
);

  wire N1, N2, N3, N4, N5, N7, N8;

  Decoder #(.enable("false"), .select(3), .tristate("false")) decoder_1 (
    .out0(N1), .out1(N2), .out2(N3), .out3(N4), .out4(N5), .out5(result), .out6(N7), .out7(N8), .sel(3'b101));

  assign halt = 1'b1;

  // Other names for the same wires on the sheet: N6 = result
endmodule
