// Logisim project select-Encoder.circ as structural Verilog: 1 circuit, main circuit main
module main (
  output [2:0] result,
  output halt
);

  wire N9;

  Priority_Encoder #(.disabled(0), .select(3)) priority_encoder_1 (
    .in0(1'b0), .in1(1'b0), .in2(1'b0), .in3(1'b0), .in4(1'b0), .in5(1'b1), .in6(1'b0), .in7(1'b0),
    .out(result), .en_in(1'b1), .gs(N9));  // open: en_out

  assign halt = 1'b1;

  // Other names for the same wires on the sheet: N8[2:0] = result
endmodule
