// Logisim project select-Mux.circ as structural Verilog: 1 circuit, main circuit main
module main (
  output result,
  output halt
);

  Multiplexer #(.enable("false"), .select(3), .tristate("false"), .width(1)) multiplexer_1 (
    .in0(1'b0), .in1(1'b0), .in2(1'b0), .in3(1'b0), .in4(1'b0), .in5(1'b1), .in6(1'b0), .in7(1'b0),
    .out(result), .sel(3'b101));

  assign halt = 1'b1;

  // Other names for the same wires on the sheet: N9 = result
endmodule
