// Logisim project sequence-DFF.circ as structural Verilog: 2 circuits, main circuit main
module main (
  output [7:0] result,
  output halt
);

  wire N0;
  wire [3:0] N3;

  Clock #(.highDuration(1), .lowDuration(1), .width(1)) clock_1 (.out(N0));
  Counter #(.max('h3), .ongoal("wrap"), .trigger("rising"), .width(4)) counter_1 (
    .load(1'b0), .D(4'b0000), .count(1'b1), .Q(N3), .carry(halt), .clk(N0), .clr(1'b0));
  Practice_RegisterBits_p8 practice_registerbits_p8_1 (.D(8'ha5), .CLK(N0), .CLR(1'b0), .Q(result));

  // Other names for the same wires on the sheet: N4 = halt; N6[7:0] = result
endmodule

module Practice_RegisterBits_p8 (
  input  [7:0] D,
  input  CLK,
  input  CLR,
  output [7:0] Q
);

  D_Flip_Flop #(.trigger("rising"), .width(1)) d_ff_1 (
    .clk(CLK), .D(D[2]), .Q(Q[2]), .preset(1'b0), .en(1'b1), .reset(CLR));  // open: Qn
  D_Flip_Flop #(.trigger("rising"), .width(1)) d_ff_2 (
    .clk(CLK), .D(D[3]), .Q(Q[3]), .preset(1'b0), .en(1'b1), .reset(CLR));  // open: Qn
  D_Flip_Flop #(.trigger("rising"), .width(1)) d_ff_3 (
    .clk(CLK), .D(D[4]), .Q(Q[4]), .preset(1'b0), .en(1'b1), .reset(CLR));  // open: Qn
  D_Flip_Flop #(.trigger("rising"), .width(1)) d_ff_4 (
    .clk(CLK), .D(D[5]), .Q(Q[5]), .preset(1'b0), .en(1'b1), .reset(CLR));  // open: Qn
  D_Flip_Flop #(.trigger("rising"), .width(1)) d_ff_5 (
    .clk(CLK), .D(D[6]), .Q(Q[6]), .preset(1'b0), .en(1'b1), .reset(CLR));  // open: Qn
  D_Flip_Flop #(.trigger("rising"), .width(1)) d_ff_6 (
    .clk(CLK), .D(D[7]), .Q(Q[7]), .preset(1'b0), .en(1'b1), .reset(CLR));  // open: Qn
  D_Flip_Flop #(.trigger("rising"), .width(1)) d_ff_7 (
    .clk(CLK), .D(D[0]), .Q(Q[0]), .preset(1'b0), .en(1'b1), .reset(CLR));  // open: Qn
  D_Flip_Flop #(.trigger("rising"), .width(1)) d_ff_8 (
    .clk(CLK), .D(D[1]), .Q(Q[1]), .preset(1'b0), .en(1'b1), .reset(CLR));  // open: Qn

  // Other names for the same wires on the sheet: N0[7:0] = D; N4 = D[0]; N5 = D[1]; N6 = D[2]; N7 = D[3]; N8 = D[4];
  //   N9 = D[5]; N10 = D[6]; N11 = D[7]; N1 = CLK; N2 = CLR; N3[7:0] = Q; N12 = Q[0]; N13 = Q[1]; N14 = Q[2];
  //   N15 = Q[3]; N16 = Q[4]; N17 = Q[5]; N18 = Q[6]; N19 = Q[7]
endmodule
