// Logisim project sequence-RAM.circ as structural Verilog: 2 circuits, main circuit main
module main (
  output [7:0] result,
  output halt
);

  wire N0;
  wire [3:0] N3;

  Clock #(.highDuration(1), .lowDuration(1), .width(1)) clock_1 (.out(N0));
  Counter #(.max('h3), .ongoal("wrap"), .trigger("rising"), .width(4)) counter_1 (
    .load(1'b0), .D(4'b0000), .count(1'b1), .Q(N3), .carry(halt), .clk(N0), .clr(1'b0));
  Practice_InitializedRAM_p8 practice_initializedram_p8_1 (.ADDR(4'b0000), .D(8'h5a), .WE(1'b1), .CLK(N0), .Q(result));

  // Other names for the same wires on the sheet: N4 = halt; N7[7:0] = result
endmodule

module Practice_InitializedRAM_p8 (
  input  [3:0] ADDR,
  input  [7:0] D,
  input  WE,
  input  CLK,
  output [7:0] Q
);

  wire N8;
  wire [7:0] N5, N6;

  Multiplexer #(.enable("false"), .select(1), .tristate("false"), .width(8)) multiplexer_1 (
    .in0(N5), .in1(N6), .out(Q), .sel(N8));
  ROM #(.addrWidth(4), .dataWidth(8)) \u_初始内容  (.addr(ADDR), .data(N5), .sel(1'b1));
  RAM #(.addrWidth(4), .bus("separate"), .dataWidth(8)) \u_运行写入  (
    .addr(ADDR), .din(D), .data(N6), .str(WE), .sel(1'b1), .clk(CLK), .ld(1'b1), .clr(1'b0));
  RAM #(.addrWidth(4), .bus("separate"), .dataWidth(1)) \u_地址已写标记  (
    .addr(ADDR), .din(1'b1), .data(N8), .str(WE), .sel(1'b1), .clk(CLK), .ld(1'b1), .clr(1'b0));

  // Other names for the same wires on the sheet: N0[3:0] = ADDR; N1[7:0] = D; N2 = WE; N3 = CLK; N4[7:0] = Q

  // Notes on the sheet:
  //   contents of 初始内容 (hex, n*v repeats v):
  //   a5
endmodule
