// Logisim project sequence-SRFF.circ as structural Verilog: 1 circuit, main circuit main
module main (
  output result,
  output halt
);

  wire N0;
  wire [3:0] N3;

  Clock #(.highDuration(1), .lowDuration(1), .width(1)) clock_1 (.out(N0));
  Counter #(.max('h3), .ongoal("wrap"), .trigger("rising"), .width(4)) counter_1 (
    .load(1'b0), .D(4'b0000), .count(1'b1), .Q(N3), .carry(halt), .clk(N0), .clr(1'b0));
  S_R_Flip_Flop #(.trigger("rising"), .width(1)) s_r_ff_1 (
    .S(1'b1), .clk(N0), .R(1'b0), .Q(result), .preset(1'b0), .reset(1'b0), .en(1'b1));  // open: Qn

  // Other names for the same wires on the sheet: N4 = halt; N5 = result
endmodule
