// Logisim project sequence-ShiftRegister.circ as structural Verilog: 2 circuits, main circuit main
module main (
  output [3:0] result,
  output halt
);

  wire N0;
  wire [3:0] N3;

  Clock #(.highDuration(1), .lowDuration(1), .width(1)) clock_1 (.out(N0));
  Counter #(.max('h3), .ongoal("wrap"), .trigger("rising"), .width(4)) counter_1 (
    .load(1'b0), .D(4'b0000), .count(1'b1), .Q(N3), .carry(halt), .clk(N0), .clr(1'b0));
  Practice_RegisterBits_p8 practice_registerbits_p8_1 (.D(1'b1), .CLK(N0), .CLR(1'b0), .Q(result));

  // Other names for the same wires on the sheet: N4 = halt; N6[3:0] = result
endmodule

module Practice_RegisterBits_p8 (
  input  D,
  input  CLK,
  input  CLR,
  output [3:0] Q
);

  D_Flip_Flop #(.trigger("rising"), .width(1)) d_ff_1 (
    .clk(CLK), .D(Q[2]), .Q(Q[3]), .preset(1'b0), .en(1'b1), .reset(CLR));  // open: Qn
  D_Flip_Flop #(.trigger("rising"), .width(1)) d_ff_2 (
    .clk(CLK), .D(D), .Q(Q[0]), .preset(1'b0), .en(1'b1), .reset(CLR));  // open: Qn
  D_Flip_Flop #(.trigger("rising"), .width(1)) d_ff_3 (
    .clk(CLK), .D(Q[0]), .Q(Q[1]), .preset(1'b0), .en(1'b1), .reset(CLR));  // open: Qn
  D_Flip_Flop #(.trigger("rising"), .width(1)) d_ff_4 (
    .clk(CLK), .D(Q[1]), .Q(Q[2]), .preset(1'b0), .en(1'b1), .reset(CLR));  // open: Qn

  // Other names for the same wires on the sheet: N0 = D; N1 = CLK; N2 = CLR; N3[3:0] = Q; N4 = Q[0]; N5 = Q[1];
  //   N6 = Q[2]; N7 = Q[3]
endmodule
