// Logisim project three-level-custom-interface.circ as structural Verilog: 3 circuits, main circuit main
module main (
  output [7:0] result,
  output halt
);

  \中层  \u_中层_1  (.\输入 (8'ha5), .\输出 (result));

  assign halt = 1'b1;

  // Other names for the same wires on the sheet: N1[7:0] = result
endmodule

module \底层非门  (
  input  [7:0] \输入 ,
  output [7:0] \输出 
);

  assign \输出  = ~\输入 ;  // NOT_Gate not_1, 8 bits wide

  // Other names for the same wires on the sheet: N0[7:0] = \输入 ; N1[7:0] = \输出 
endmodule

module \中层  (
  input  [7:0] \输入 ,
  output [7:0] \输出 
);

  \底层非门  \u_底层非门_1  (.\输入 (\输入 ), .\输出 (\输出 ));

  // Other names for the same wires on the sheet: N0[7:0] = \输入 ; N1[7:0] = \输出 
endmodule
