// Logisim project logisim-limited.circ as structural Verilog: 1 circuit, main circuit main
module main (
  input  A,
  input  Select,
  input  B,
  output Q
);

  wire Carry_out, CLK_out, Mux_out, Sum_out;
  wire [7:0] \未支持示例_out ;

  xor Sum (Sum_out, A, B);
  and Carry (Carry_out, A, B);
  Multiplexer #(.enable("false")) Mux (.in0(Sum_out), .in1(Carry_out), .out(Mux_out), .sel(Select));
  Adder #(.width(8)) \u_未支持示例  (.out(\未支持示例_out ));  // open: a, b, cin, cout
  Clock CLK (.out(CLK_out));
  Register #(.width(1)) Stored (.D(Mux_out), .Q(Q), .clk(CLK_out));  // open: en, clr
endmodule
